// Logisim project cpu.circ as structural Verilog
module full_adder (
  input  IN_A,
  input  IN_B,
  input  IN_Carry,
  output Out_Carry,
  output Sum
);

  wire and_1_out, and_2_out, and_3_out;

  and and_1 (and_1_out, IN_A, IN_B);
  and and_2 (and_2_out, IN_A, IN_Carry);
  and and_3 (and_3_out, IN_B, IN_Carry);
  xor xor_1 (Sum, IN_A, IN_B, IN_Carry);
  or or_1 (Out_Carry, and_1_out, and_2_out, and_3_out);
endmodule

module adder4 (
  input  [3:0] IN_A,
  input  [3:0] IN_B,
  input  IN_Carry,
  output Out_Carry,
  output b3,
  output b2,
  output b1,
  output b0
);

  wire full_adder_2_out_carry, full_adder_3_out_carry, full_adder_4_out_carry;

  full_adder full_adder_1 (
    .IN_A(IN_A[3]), .IN_B(IN_B[3]), .IN_Carry(full_adder_2_out_carry), .Out_Carry(Out_Carry), .Sum(b3));
  full_adder full_adder_2 (
    .IN_A(IN_A[2]), .IN_B(IN_B[2]), .IN_Carry(full_adder_3_out_carry), .Out_Carry(full_adder_2_out_carry),
    .Sum(b2));
  full_adder full_adder_3 (
    .IN_A(IN_A[1]), .IN_B(IN_B[1]), .IN_Carry(full_adder_4_out_carry), .Out_Carry(full_adder_3_out_carry),
    .Sum(b1));
  full_adder full_adder_4 (
    .IN_A(IN_A[0]), .IN_B(IN_B[0]), .IN_Carry(IN_Carry), .Out_Carry(full_adder_4_out_carry), .Sum(b0));
endmodule

module adder16 (
  input  [15:0] IN_A,
  input  [15:0] IN_B,
  input  IN_Carry,
  output Out_Carry,
  output [15:0] Sum
);

  wire adder4_2_out_carry, adder4_3_out_carry, adder4_4_out_carry;

  adder4 adder4_1 (
    .IN_A(IN_A[15:12]), .IN_B(IN_B[15:12]), .IN_Carry(adder4_2_out_carry), .Out_Carry(Out_Carry),
    .b3(Sum[15]), .b2(Sum[14]), .b1(Sum[13]), .b0(Sum[12]));
  adder4 adder4_2 (
    .IN_A(IN_A[11:8]), .IN_B(IN_B[11:8]), .IN_Carry(adder4_3_out_carry), .Out_Carry(adder4_2_out_carry),
    .b3(Sum[11]), .b2(Sum[10]), .b1(Sum[9]), .b0(Sum[8]));
  adder4 adder4_3 (
    .IN_A(IN_A[7:4]), .IN_B(IN_B[7:4]), .IN_Carry(adder4_4_out_carry), .Out_Carry(adder4_3_out_carry),
    .b3(Sum[7]), .b2(Sum[6]), .b1(Sum[5]), .b0(Sum[4]));
  adder4 adder4_4 (
    .IN_A(IN_A[3:0]), .IN_B(IN_B[3:0]), .IN_Carry(IN_Carry), .Out_Carry(adder4_4_out_carry), .b3(Sum[3]),
    .b2(Sum[2]), .b1(Sum[1]), .b0(Sum[0]));
endmodule

module subtractor16 (
  input  [15:0] IN_A,
  input  [15:0] IN_B,
  output [15:0] Sum
);

  wire [15:0] not_1_out;

  assign not_1_out = ~IN_B;  // NOT_Gate not_1, 16 bits wide
  adder16 adder16_1 (.IN_A(IN_A), .IN_B(not_1_out), .IN_Carry(1'b1), .Sum(Sum));  // open: Out_Carry
endmodule

module ALU (
  input  [2:0] Operation,
  input  [15:0] IN_A,
  input  [15:0] IN_B,
  output Out_Carry,
  output [15:0] Result
);

  wire [15:0] adder16_1_sum, and_1_out, left_bit_shifter16_1_result, not_1_out, or_1_out,
       right_bit_shifter16_1_result, subtractor16_1_sum;

  adder16 adder16_1 (.IN_A(IN_A), .IN_B(IN_B), .IN_Carry(1'b0), .Out_Carry(Out_Carry), .Sum(adder16_1_sum));
  subtractor16 subtractor16_1 (.IN_A(IN_A), .IN_B(IN_B), .Sum(subtractor16_1_sum));
  left_bit_shifter16 left_bit_shifter16_1 (.IN_A(IN_A), .Result(left_bit_shifter16_1_result));
  right_bit_shifter16 right_bit_shifter16_1 (.IN_A(IN_A), .Result(right_bit_shifter16_1_result));
  assign and_1_out = IN_A & IN_B;  // AND_Gate and_1, 16 bits wide
  assign or_1_out = IN_A | IN_B;  // OR_Gate or_1, 16 bits wide
  assign not_1_out = ~IN_A;  // NOT_Gate not_1, 16 bits wide
  multiplexer16_8x1 multiplexer16_8x1_1 (
    .Addr(Operation), .IN_0(adder16_1_sum), .IN_1(subtractor16_1_sum), .IN_2(left_bit_shifter16_1_result),
    .IN_3(right_bit_shifter16_1_result), .IN_4(and_1_out), .IN_5(or_1_out), .IN_6(not_1_out), .Result(Result));  // open: IN_7
endmodule

module left_bit_shifter16 (
  input  [15:0] IN_A,
  output [15:0] Result
);


  assign Result = {IN_A[14:0], 1'b0};
  // also tied to GND on the sheet: IN_A[15]
endmodule

module right_bit_shifter16 (
  input  [15:0] IN_A,
  output [15:0] Result
);


  assign Result = {1'b0, IN_A[15:1]};
  // also tied to GND on the sheet: IN_A[0]
endmodule

module decoder_1x8 (
  input  [2:0] IN_A,
  output Out_0,
  output Out_1,
  output Out_2,
  output Out_3,
  output Out_4,
  output Out_5,
  output Out_6,
  output Out_7
);

  and and_1 (Out_0, ~IN_A[2], ~IN_A[1], ~IN_A[0]);  // AND_Gate
  and and_2 (Out_1, ~IN_A[2], ~IN_A[1], IN_A[0]);  // AND_Gate
  and and_3 (Out_2, ~IN_A[2], IN_A[1], ~IN_A[0]);  // AND_Gate
  and and_4 (Out_3, ~IN_A[2], IN_A[1], IN_A[0]);  // AND_Gate
  and and_5 (Out_4, IN_A[2], ~IN_A[1], ~IN_A[0]);  // AND_Gate
  and and_6 (Out_5, IN_A[2], ~IN_A[1], IN_A[0]);  // AND_Gate
  and and_7 (Out_6, IN_A[2], IN_A[1], ~IN_A[0]);  // AND_Gate
  and and_8 (Out_7, IN_A[2], IN_A[1], IN_A[0]);
endmodule

module multiplexer16_8x1 (
  input  [2:0] Addr,
  input  [15:0] IN_0,
  input  [15:0] IN_1,
  input  [15:0] IN_2,
  input  [15:0] IN_3,
  input  [15:0] IN_4,
  input  [15:0] IN_5,
  input  [15:0] IN_6,
  input  [15:0] IN_7,
  output [15:0] Result
);

  wire decoder_1x8_1_out_0, decoder_1x8_1_out_1, decoder_1x8_1_out_2, decoder_1x8_1_out_3,
       decoder_1x8_1_out_4, decoder_1x8_1_out_5, decoder_1x8_1_out_6, decoder_1x8_1_out_7;

  decoder_1x8 decoder_1x8_1 (
    .IN_A(Addr), .Out_0(decoder_1x8_1_out_0), .Out_1(decoder_1x8_1_out_1), .Out_2(decoder_1x8_1_out_2),
    .Out_3(decoder_1x8_1_out_3), .Out_4(decoder_1x8_1_out_4), .Out_5(decoder_1x8_1_out_5),
    .Out_6(decoder_1x8_1_out_6), .Out_7(decoder_1x8_1_out_7));
  assign Result = decoder_1x8_1_out_0 ? IN_0 : 16'bz;  // Controlled_Buffer controlled_buffer_1
  assign Result = decoder_1x8_1_out_1 ? IN_1 : 16'bz;  // Controlled_Buffer controlled_buffer_2
  assign Result = decoder_1x8_1_out_2 ? IN_2 : 16'bz;  // Controlled_Buffer controlled_buffer_3
  assign Result = decoder_1x8_1_out_3 ? IN_3 : 16'bz;  // Controlled_Buffer controlled_buffer_4
  assign Result = decoder_1x8_1_out_4 ? IN_4 : 16'bz;  // Controlled_Buffer controlled_buffer_5
  assign Result = decoder_1x8_1_out_5 ? IN_5 : 16'bz;  // Controlled_Buffer controlled_buffer_6
  assign Result = decoder_1x8_1_out_6 ? IN_6 : 16'bz;  // Controlled_Buffer controlled_buffer_7
  assign Result = decoder_1x8_1_out_7 ? IN_7 : 16'bz;  // Controlled_Buffer controlled_buffer_8
endmodule

module d_flip_flop (
  input  EN,
  input  S,
  output Q
);

  wire and_1_out, and_2_out, nor_2_out, not_1_out;

  not not_1 (not_1_out, S);
  and and_1 (and_1_out, not_1_out, EN);
  and and_2 (and_2_out, EN, S);
  nor nor_1 (Q, and_1_out, nor_2_out);
  nor nor_2 (nor_2_out, Q, and_2_out);
endmodule

module register16 (
  input  [15:0] IN_Data,
  input  EN,
  input  LD,
  output [15:0] OUT_Data
);

  wire [15:0] d_flip_flop_16_q;

  d_flip_flop d_flip_flop_1 (.EN(EN), .S(IN_Data[15]), .Q(d_flip_flop_16_q[15]));
  d_flip_flop d_flip_flop_2 (.EN(EN), .S(IN_Data[14]), .Q(d_flip_flop_16_q[14]));
  d_flip_flop d_flip_flop_3 (.EN(EN), .S(IN_Data[13]), .Q(d_flip_flop_16_q[13]));
  d_flip_flop d_flip_flop_4 (.EN(EN), .S(IN_Data[12]), .Q(d_flip_flop_16_q[12]));
  d_flip_flop d_flip_flop_5 (.EN(EN), .S(IN_Data[11]), .Q(d_flip_flop_16_q[11]));
  d_flip_flop d_flip_flop_6 (.EN(EN), .S(IN_Data[10]), .Q(d_flip_flop_16_q[10]));
  d_flip_flop d_flip_flop_7 (.EN(EN), .S(IN_Data[9]), .Q(d_flip_flop_16_q[9]));
  d_flip_flop d_flip_flop_8 (.EN(EN), .S(IN_Data[8]), .Q(d_flip_flop_16_q[8]));
  d_flip_flop d_flip_flop_9 (.EN(EN), .S(IN_Data[7]), .Q(d_flip_flop_16_q[7]));
  d_flip_flop d_flip_flop_10 (.EN(EN), .S(IN_Data[6]), .Q(d_flip_flop_16_q[6]));
  d_flip_flop d_flip_flop_11 (.EN(EN), .S(IN_Data[5]), .Q(d_flip_flop_16_q[5]));
  d_flip_flop d_flip_flop_12 (.EN(EN), .S(IN_Data[4]), .Q(d_flip_flop_16_q[4]));
  d_flip_flop d_flip_flop_13 (.EN(EN), .S(IN_Data[3]), .Q(d_flip_flop_16_q[3]));
  d_flip_flop d_flip_flop_14 (.EN(EN), .S(IN_Data[2]), .Q(d_flip_flop_16_q[2]));
  d_flip_flop d_flip_flop_15 (.EN(EN), .S(IN_Data[1]), .Q(d_flip_flop_16_q[1]));
  d_flip_flop d_flip_flop_16 (.EN(EN), .S(IN_Data[0]), .Q(d_flip_flop_16_q[0]));
  assign OUT_Data = LD ? d_flip_flop_16_q : 16'bz;  // Controlled_Buffer controlled_buffer_1
endmodule

module RegisterFile8 (
  input  [15:0] IN_Data,
  input  [2:0] WriteAddr,
  input  [2:0] ReadAddr1,
  input  [2:0] ReadAddr2,
  input  in_5,
  output [15:0] DataOut1,
  output [15:0] DataOut2
);

  wire decoder_1x8_1_out_0, decoder_1x8_1_out_1, decoder_1x8_1_out_2, decoder_1x8_1_out_3,
       decoder_1x8_1_out_4, decoder_1x8_1_out_5, decoder_1x8_1_out_6, decoder_1x8_1_out_7;
  wire [15:0] register16_1_out_data, register16_2_out_data, register16_3_out_data, register16_4_out_data,
       register16_5_out_data, register16_6_out_data, register16_7_out_data, register16_8_out_data;

  decoder_1x8 decoder_1x8_1 (
    .IN_A(WriteAddr), .Out_0(decoder_1x8_1_out_0), .Out_1(decoder_1x8_1_out_1), .Out_2(decoder_1x8_1_out_2),
    .Out_3(decoder_1x8_1_out_3), .Out_4(decoder_1x8_1_out_4), .Out_5(decoder_1x8_1_out_5),
    .Out_6(decoder_1x8_1_out_6), .Out_7(decoder_1x8_1_out_7));
  register16 register16_1 (.IN_Data(IN_Data), .EN(decoder_1x8_1_out_0), .LD(in_5), .OUT_Data(register16_1_out_data));
  register16 register16_2 (.IN_Data(IN_Data), .EN(decoder_1x8_1_out_1), .LD(in_5), .OUT_Data(register16_2_out_data));
  register16 register16_3 (.IN_Data(IN_Data), .EN(decoder_1x8_1_out_2), .LD(in_5), .OUT_Data(register16_3_out_data));
  register16 register16_4 (.IN_Data(IN_Data), .EN(decoder_1x8_1_out_3), .LD(in_5), .OUT_Data(register16_4_out_data));
  register16 register16_5 (.IN_Data(IN_Data), .EN(decoder_1x8_1_out_4), .LD(in_5), .OUT_Data(register16_5_out_data));
  register16 register16_6 (.IN_Data(IN_Data), .EN(decoder_1x8_1_out_5), .LD(in_5), .OUT_Data(register16_6_out_data));
  register16 register16_7 (.IN_Data(IN_Data), .EN(decoder_1x8_1_out_6), .LD(in_5), .OUT_Data(register16_7_out_data));
  register16 register16_8 (.IN_Data(IN_Data), .EN(decoder_1x8_1_out_7), .LD(in_5), .OUT_Data(register16_8_out_data));
  multiplexer16_8x1 multiplexer16_8x1_1 (
    .Addr(ReadAddr1), .IN_0(register16_1_out_data), .IN_1(register16_2_out_data),
    .IN_2(register16_3_out_data), .IN_3(register16_4_out_data), .IN_4(register16_5_out_data),
    .IN_5(register16_6_out_data), .IN_6(register16_7_out_data), .IN_7(register16_8_out_data),
    .Result(DataOut1));
  multiplexer16_8x1 multiplexer16_8x1_2 (
    .Addr(ReadAddr2), .IN_0(register16_1_out_data), .IN_1(register16_2_out_data),
    .IN_2(register16_3_out_data), .IN_3(register16_4_out_data), .IN_4(register16_5_out_data),
    .IN_5(register16_6_out_data), .IN_6(register16_7_out_data), .IN_7(register16_8_out_data),
    .Result(DataOut2));
endmodule

module demultiplexer16_1x8 (
  input  [15:0] DataIn,
  input  [2:0] Addr,
  output [15:0] out_3,
  output [15:0] out_4,
  output [15:0] out_5,
  output [15:0] out_6,
  output [15:0] out_7,
  output [15:0] out_8,
  output [15:0] out_9,
  output [15:0] out_10
);

  wire decoder_1x8_1_out_0, decoder_1x8_1_out_1, decoder_1x8_1_out_2, decoder_1x8_1_out_3,
       decoder_1x8_1_out_4, decoder_1x8_1_out_5, decoder_1x8_1_out_6, decoder_1x8_1_out_7;

  decoder_1x8 decoder_1x8_1 (
    .IN_A(Addr), .Out_0(decoder_1x8_1_out_0), .Out_1(decoder_1x8_1_out_1), .Out_2(decoder_1x8_1_out_2),
    .Out_3(decoder_1x8_1_out_3), .Out_4(decoder_1x8_1_out_4), .Out_5(decoder_1x8_1_out_5),
    .Out_6(decoder_1x8_1_out_6), .Out_7(decoder_1x8_1_out_7));
  assign out_3 = decoder_1x8_1_out_0 ? DataIn : 16'bz;  // Controlled_Buffer controlled_buffer_1
  assign out_4 = decoder_1x8_1_out_1 ? DataIn : 16'bz;  // Controlled_Buffer controlled_buffer_2
  assign out_5 = decoder_1x8_1_out_2 ? DataIn : 16'bz;  // Controlled_Buffer controlled_buffer_3
  assign out_6 = decoder_1x8_1_out_3 ? DataIn : 16'bz;  // Controlled_Buffer controlled_buffer_4
  assign out_7 = decoder_1x8_1_out_4 ? DataIn : 16'bz;  // Controlled_Buffer controlled_buffer_5
  assign out_8 = decoder_1x8_1_out_5 ? DataIn : 16'bz;  // Controlled_Buffer controlled_buffer_6
  assign out_9 = decoder_1x8_1_out_6 ? DataIn : 16'bz;  // Controlled_Buffer controlled_buffer_7
  assign out_10 = decoder_1x8_1_out_7 ? DataIn : 16'bz;  // Controlled_Buffer controlled_buffer_8
endmodule
